# Fritzing sketch example-write-schematic (saved by Fritzing 0.5.2b)
breadboards: 1

parts:
  Arduino1 = Arduino
  4051 = IC, DIP package, 16 pins [chip_label=IC spacing=300mil]
  R1 = Resistor [resistance=330 package=THT]
  LED1 = Red LED - 5mm [package="5 mm [THT]"]
  R2 = Resistor [resistance=330 package=THT]
  R3 = Resistor [resistance=330 package=THT]
  LED2 = Red LED - 5mm [package="5 mm [THT]"]
  LED3 = Red LED - 5mm [package="5 mm [THT]"]

nets:
  N1: Arduino1.GND, 4051.pin7, 4051.pin8, LED1.cathode, LED2.cathode, LED3.cathode
  N2: Arduino1.D6, 4051.pin3
  N3: Arduino1.D4, 4051.pin11
  N4: Arduino1.D3, 4051.pin10
  N5: Arduino1.D2, 4051.pin9
  N6: Arduino1.+5V, 4051.pin6, 4051.pin16
  N7: 4051.pin13, R1.Pin_1
  N8: 4051.pin14, R2.Pin_0
  N9: 4051.pin15, R3.Pin_0
  N10: R1.Pin_0, LED1.anode
  N11: R2.Pin_1, LED2.anode
  N12: R3.Pin_1, LED3.anode
